# Fritzing sketch Untitled Sketch (saved by Fritzing 0.9.3b)
breadboards: 1

parts:
  Componente1 = Arduino Mega 2560 (Rev3)
  LED1 = LED - 3mm [color="Red (633nm)" package="3 mm [THT]"]
  hc-sr1 = hc-sr04
  J2 = Basic Servo
  R1 = Resistor [tolerance=±5% resistance=220 package=THT]
  J3 = Basic Servo

nets:
  N1: Componente1.D8_PWM, J2.pulse
  VCC: Componente1.5V, hc-sr1.VCC, J2.vcc, J3.vcc
  GND: Componente1.GND, hc-sr1.GND, J2.gnd, R1.Pin_0, J3.gnd
  N2: Componente1.D2_PWM, LED1.anode
  N3: Componente1.D3_PWM, hc-sr1.Trig
  N4: Componente1.D4_PWM, hc-sr1.Echo
  N5: Componente1.D7_PWM, J3.pulse
  N6: LED1.cathode, R1.Pin_1
